# Fritzing sketch button_fritz (saved by Fritzing 0.9.2b)
breadboards: 1

parts:
  R1 = Resistor [tolerance=±5% resistance=10k package=THT]
  S1 = Pushbutton [package="[SMD]"]
  Part1 = Arduino Uno (Rev3)

nets:
  N1: R1.Pin_0, S1.Pin_1, S1.Pin_2, Part1.D2
  N2: R1.Pin_1, Part1.GND
  N3: S1.Pin_3, S1.Pin_4, Part1.5V
